# Fritzing sketch VGA (saved by Fritzing 0.9.2b)
breadboards: 1

parts:
  R1 = Resistor [tolerance=±10% resistance=330 package=THT]
  R2 = Resistor [tolerance=±10% resistance=100 package=THT]

nets:
  Espruino A7: R1.Pin_0
  VGA Pins 1,2 and 3 (R,G and B): R1.Pin_1, R2.Pin_0
  Espruino GND/VGA Pins 5,6,7,8,9,10 (GND): R2.Pin_1
